// Logisim project ALU.circ as structural Verilog: 1 circuit, main circuit ALU
module ALU (
  input  [31:0] A,
  input  [31:0] B,
  input  [4:0] Shift,
  input  [3:0] Codop,
  input  CarryIn,
  output [31:0] S,
  output [3:0] Flags
);

  wire adder_2_cout, bitselector_3_out, bitselector_4_out, bitselector_5_out, bitselector_6_out,
       bitselector_7_out, Bout, comparator_1_eq, comparator_2_eq, comparator_4_eq, Cout, not_2_out,
       not_4_out, not_5_out, not_6_out, not_7_out, opShift, SigneA, SigneB, vADD, vSUB;
  wire [3:0] subtractor_5_out;
  wire [4:0] subtractor_3_out, subtractor_4_out;
  wire [31:0] AandB, AfoisB, AorB, AplusBplusCin, AXorB, BandNotA, BmoinsAplusCinMoins1, BShiftArithmetic,
       BShiftLeft, BShiftRight, BShiftRotRight, not_1_out, notA, ZeromoinsA;

  assign not_1_out = ~A;  // NOT_Gate not_1, 32 bits wide
  assign AandB = A & B;  // AND_Gate and_1, 32 bits wide
  assign AXorB = A ^ B;  // XOR_Gate xor_1, 32 bits wide
  Shifter #(.width(32)) shifter_1 (.in(B), .\dist (Shift), .out(BShiftLeft));
  Shifter #(.shift("lr"), .width(32)) shifter_2 (.in(B), .\dist (Shift), .out(BShiftRight));
  Shifter #(.shift("ar"), .width(32)) shifter_3 (.in(B), .\dist (Shift), .out(BShiftArithmetic));
  Adder #(.width(32)) adder_1 (.a(A), .b(B), .out(AplusBplusCin), .cin(CarryIn), .cout(Cout));
  not not_2 (not_2_out, CarryIn);
  Subtractor #(.width(32)) subtractor_1 (.a(B), .b(A), .out(BmoinsAplusCinMoins1), .bin(not_2_out), .bout(Bout));
  Shifter #(.shift("rr"), .width(32)) shifter_4 (.in(B), .\dist (Shift), .out(BShiftRotRight));
  Subtractor #(.width(32)) subtractor_2 (.a({32{1'b0}}), .b(A), .out(ZeromoinsA));  // open: bin, bout
  assign AorB = A | B;  // OR_Gate or_1, 32 bits wide
  Multiplier #(.width(32)) multiplier_1 (.a(A), .b(B), .out(AfoisB));  // open: cin, cout
  assign BandNotA = not_1_out & B;  // AND_Gate and_2, 32 bits wide
  assign notA = ~A;  // NOT_Gate not_3, 32 bits wide
  BitSelector #(.width(32)) bitselector_1 (.in(A), .out(SigneA), .sel(5'b00001));
  BitSelector #(.width(32)) bitselector_2 (.in(B), .out(SigneB), .sel(5'b00001));
  Multiplexer #(.select(4), .width(32)) multiplexer_1 (
    .in0(AandB), .in1(AXorB), .in2(BShiftLeft), .in3(BShiftRight), .in4(BShiftArithmetic),
    .in5(AplusBplusCin), .in6(BmoinsAplusCinMoins1), .in7(BShiftRotRight), .in8(B), .in9(ZeromoinsA),
    .in10(B), .in11(B), .in12(AorB), .in13(AfoisB), .in14(BandNotA), .in15(notA), .out({Flags[3], S[30:0]}),
    .sel(Codop));
  Adder #(.width(32)) adder_2 (.a(notA), .b(32'h1), .cout(adder_2_cout));  // open: out, cin
  Subtractor #(.width(5)) subtractor_3 (.a({5{1'b0}}), .b(Shift), .out(subtractor_3_out));  // open: bin, bout
  Subtractor #(.width(5)) subtractor_4 (.a(Shift), .b(5'b00001), .out(subtractor_4_out));  // open: bin, bout
  not not_4 (not_4_out, Bout);
  BitSelector #(.width(32)) bitselector_3 (.in(B), .out(bitselector_3_out), .sel(subtractor_4_out));
  BitSelector #(.width(32)) bitselector_4 (.in(B), .out(bitselector_4_out), .sel(subtractor_3_out));
  Comparator #(.width(1)) comparator_1 (.a(SigneA), .b(SigneB), .eq(comparator_1_eq));  // open: gt, lt
  BitSelector #(.width(32)) bitselector_5 (.in(AplusBplusCin), .out(bitselector_5_out), .sel(5'b00001));
  Multiplexer #(.enable("true"), .select(4)) multiplexer_2 (
    .in0(1'b0), .in1(1'b0), .in2(opShift), .in3(opShift), .in4(1'b0), .in5(Cout), .in6(not_4_out),
    .in7(1'b0), .in8(1'b0), .in9(adder_2_cout), .in10(not_4_out), .in11(Cout), .in12(1'b0), .in13(1'b0),
    .in14(1'b0), .in15(1'b0), .out(Flags[1]), .sel(Codop));  // open: en
  Multiplexer multiplexer_3 (.in0(bitselector_3_out), .in1(bitselector_4_out), .out(opShift), .sel(bitselector_6_out));
  Subtractor #(.width(4)) subtractor_5 (.a(Codop), .b(4'b0010), .out(subtractor_5_out));  // open: bin, bout
  Multiplexer #(.enable("true"), .select(4)) multiplexer_4 (
    .in0(1'b0), .in1(1'b0), .in2(1'b0), .in3(1'b0), .in4(1'b0), .in5(vADD), .in6(vSUB), .in7(1'b0),
    .in8(1'b0), .in9(1'b0), .in10(vSUB), .in11(vADD), .in12(1'b0), .in13(1'b0), .in14(1'b0), .in15(1'b0),
    .out(Flags[0]), .sel(Codop));  // open: en
  not not_5 (not_5_out, comparator_2_eq);
  Comparator #(.width(1)) comparator_2 (.a(SigneB), .b(bitselector_5_out), .eq(comparator_2_eq));  // open: gt, lt
  Comparator #(.width(31)) comparator_3 (.a({31{1'b0}}), .b(S[30:0]), .eq(Flags[2]));  // open: gt, lt
  BitSelector #(.width(4)) bitselector_6 (.in(subtractor_5_out), .out(bitselector_6_out), .sel(2'b00));
  not not_6 (not_6_out, comparator_1_eq);
  and and_3 (vADD, comparator_1_eq, not_5_out);
  BitSelector #(.width(32)) bitselector_7 (.in(BmoinsAplusCinMoins1), .out(bitselector_7_out), .sel(5'b00001));
  not not_7 (not_7_out, comparator_4_eq);
  Comparator #(.width(1)) comparator_4 (.a(SigneB), .b(bitselector_7_out), .eq(comparator_4_eq));  // open: gt, lt
  and and_4 (vSUB, not_6_out, not_7_out);

  assign S[31] = Flags[3];

  // Other names for the same wires on the sheet: AandBBis[31:0] = B; AplusB[31:0] = B; BmoinsA[31:0] = B;
  //   Cin = CarryIn; V = Flags[0]; C = Flags[1]; Z = Flags[2]; Sortie[31:0] = {Flags[3], S[30:0]}

  // Notes on the sheet:
  //   PAS CORRECT
  //   Note: for ROR, C = N
  //   Note 2: assume that shift > 0 for LSL and LSR
  //   PENSER AUX 2 DERNIERS SHIFTS
endmodule
