// Logisim project Ctl_Data_Processing.circ as structural Verilog: 2 circuits, main circuit Data_Processing
module Data_Processing (
  input  Enable,
  input  [15:0] Instruction,
  output [2:0] Rd,
  output [2:0] Rn,
  output [2:0] Rm,
  output [3:0] ALU_Opcode,
  output [3:0] Flags_Update_Mask
);

  wire C, N, V, Z;
  wire [15:10] multiplexer_1_out;

  Multiplexer #(.width(16)) multiplexer_1 (
    .in0({16{1'b0}}), .in1(Instruction), .out({multiplexer_1_out, ALU_Opcode, Rm, Rd}), .sel(Enable));
  FlagMaskDecodeur flagmaskdecodeur_1 (.N(N), .Z(Z), .C(C), .V(V));  // open: Codop
  Multiplexer #(.width(4)) multiplexer_2 (.in0(4'b0000), .in1({N, Z, C, V}), .out(Flags_Update_Mask), .sel(Enable));

  assign Rn = Rd;

  // Other names for the same wires on the sheet: Rdn[2:0] = Rd; Opcode[3:0] = ALU_Opcode

  // Notes on the sheet:
  //   Note 2: RSB instruction has Rn as 1st operand.
  //   MUL instruction has Rn as 1st operand and Rdm as 2nd operand
  //   For simplification purposes, Rm is used for 1st operand both here and in the ALU.
  //   Note: instructions that does not save the result will still have the second operand as the destination register, the ALU will copy the second register to the destination register
  //   Pull output low on Enable = 0
endmodule

module FlagMaskDecodeur (
  input  [3:0] Codop,
  output N,
  output Z,
  output C,
  output V
);

  wire and_1_out, and_2_out, and_3_out, and_4_out, and_5_out, and_6_out, and_7_out, not_1_out, not_2_out,
       not_3_out, not_4_out;

  not not_1 (not_1_out, Codop[3]);
  not not_2 (not_2_out, Codop[2]);
  not not_3 (not_3_out, Codop[1]);
  not not_4 (not_4_out, Codop[0]);
  and and_1 (and_1_out, not_1_out, Codop[2]);
  and and_2 (and_2_out, Codop[3], not_2_out, Codop[0]);
  and and_3 (and_3_out, not_2_out, Codop[1]);
  and and_4 (and_4_out, not_1_out, Codop[2], not_3_out, Codop[0]);
  and and_5 (and_5_out, not_1_out, Codop[2], Codop[1], not_4_out);
  and and_6 (and_6_out, Codop[3], not_2_out, Codop[0]);
  and and_7 (and_7_out, Codop[3], not_2_out, Codop[1]);
  or or_1 (C, and_1_out, and_2_out, and_3_out);
  or or_2 (V, and_4_out, and_5_out, and_6_out, and_7_out);

  assign N = 1'b1;
  assign Z = 1'b1;
endmodule
